# Fritzing sketch schematic (saved by Fritzing 0.9.3b)
breadboards: 1

parts:
  U1 = Onion Omega2
  R1 = Resistor [tolerance=±5% resistance=220 package=THT]
  LED1 = LED - 5mm [color="Red (633nm)" package="5 mm [THT]"]

nets:
  N1: U1.GPIO11, R1.Pin_1
  N2: U1.GND, LED1.cathode
  N3: R1.Pin_0, LED1.anode

custom parts:
  Onion Omega2: Onion Omega2 IoT Computer Omega2: - 580 Mhz MIPS CPU - 64MB RAM, Omega2+: 128MB RAM - 16MB Flash, Omega2+: 32M Flash - LEDE Linux OS - USB2.0 - 2.4GHz b/g/n WiFi - 15GPIO - 2PWM - 2 UART - 1 I2C - 1 SPI - 1 I2S - Micro-SD Card Slot (Omega2+ only)
